# Fritzing sketch Motor Current sensing copy (saved by Fritzing 0.8.7b)
breadboards: 1

parts:
  Part1 = Arduino Uno (Rev3)
  920KV_Motor1 = DJI 920 KV Motor
  M1 = ESC
  Power_plug2 = Power plug  # not connected
  Part2 = ACS712 Low Current Sensor Board v12

nets (from the breadboard view):
  N1: Part1.A0, Part2.VO
  N2: Part1.D9_PWM, M1.DATA
  GND: Part1.GND, M1.GND, Part2.GND
  5V: Part1.5V, M1.5V, Part2.5V
  N3: 920KV_Motor1.w, M1.W
  N4: 920KV_Motor1.v, M1.V
  N5: 920KV_Motor1.u, Part2.IP-
  N6: M1.U, Part2.IP+

notes:
  BLDC
  ESC
  UNO R3
  ADAPTER INPUT - desktop power supply - variable current
  ADAPTER
  ACS712 hall effect current sensor connected to a single phase

custom parts:
  DJI 920 KV Motor: DJI Brushless Outrunner 2212/920K Motor F330-550
